# Fritzing sketch project uas fritzing (saved by Fritzing 0.9.3b)
breadboards: 2

parts:
  A1 = 2 channel relay module [package=THT]
  R1 = Resistor [tolerance=±5% resistance=220 package=THT]
  R2 = Resistor [tolerance=±5% resistance=220 package=THT]
  R3 = Resistor [tolerance=±5% resistance=220 package=THT]
  LED1 = LED - 5mm [color="Red (633nm)" package="5 mm [THT]"]
  LED2 = LED - 5mm [color="Blue (525nm)" package="5 mm [THT]"]
  LED3 = LED - 5mm [color="Green (570nm)" package="5 mm [THT]"]
  R4 = Photocell (LDR) [package=THT]
  R5 = Resistor [tolerance=±5% resistance=220 package=THT]
  KF-1 = KF-301 Relay [package=THT]
  DHT1 = DHT11 Humitidy and Temperature Sensor (3 pins)
  Part1 = SRF05 Ultrasonic Rangefinder
  J1 = Basic Servo
  YL-83_-_Detection_Board1 = YL-83 Rain Sensor - Detection Board
  U1 = NodeMCU V1.0

nets:
  N1: A1.pin_1, R3.Pin_0
  VCC: A1.pin_2, R4.pin_1, KF-1.NC, Part1.VCC, J1.vcc
  N2: A1.pin_3, A1.pin_5
  N3: A1.pin_4, R2.Pin_0
  N4: A1.pin_6, R1.Pin_0
  N5: A1.pin_13, KF-1.C, U1.Vin
  GND: A1.pin_14, LED1.cathode, LED2.cathode, LED3.cathode, R5.Pin_0, KF-1.ground, DHT1.Gnd, Part1.GND, J1.gnd, YL-83_-_Detection_Board1.POS, U1.GND
  N6: A1.pin_15, U1.D0
  N7: A1.pin_16, U1.D1
  N8: R1.Pin_1, LED3.anode
  N9: R2.Pin_1, LED2.anode
  N10: R3.Pin_1, LED1.anode
  N11: R4.pin_0, R5.Pin_1, U1.A0
  N12: KF-1.power, DHT1.Plus, U1.3V3
  N13: DHT1.Signal, U1.D3
  N14: Part1.Trig, U1.D5
  N15: Part1.Echo, U1.D6
  N16: J1.pulse, U1.D4
  N17: YL-83_-_Detection_Board1.NEG, U1.D2

custom parts:
  2 channel relay module: 2 channel Relay Module 5V 12V 24V High and Low Level Trigger Relay Control With Optocoupler Two Way relays DC 5 V 12 V 24 V Volt.
  KF-301 Relay: KF-301
  DHT11 Humitidy and Temperature Sensor (3 pins): DHT11 Humidity and Temperature Sensor (3 pins).
  YL-83 Rain Sensor - Detection Board: The YL-83 is a rain sensor that has more resistance when dry and less resistance when wet. The module runs at 5V.
  NodeMCU V1.0: ESP8266 based NodeMCU
